# Fritzing sketch cbm (saved by Fritzing 0.9.3b)
stripboards: 1

parts:
  J1 = male pin header, 4 pins [form="♂ (male)"]
  J2 = male pin header, 4 pins [form="♂ (male)"]
  R1 = Resistor [tolerance=±5% resistance=10k package=THT]
  R2 = Resistor [tolerance=±5% resistance=10k package=THT]  # not connected
  R3 = Resistor [tolerance=±5% resistance=10k package=THT]
  J3 = male pin header, 3 pins [form="♂ (male)"]
  Bauteil1 = Arduino Uno (Rev3) - ICSP
  J4 = Basic Force Sensing Resistor (FSR) [package=THT]
  J5 = Basic Force Sensing Resistor (FSR) [package=THT]
  J6 = Basic Force Sensing Resistor (FSR) [package=THT]
  Bauteil2 = NeoPixel Stick [part_number=1426]

nets:
  GND: J1.pin1, Bauteil1.GND, Bauteil2.GND
  N1: J1.pin2, R3.Pin_1, J3.pin1, Bauteil1.A2, J4.pin_1
  N2: J1.pin3, J2.pin3, R1.Pin_1, J3.pin2, Bauteil1.A1, J5.pin_1
  N3: J1.pin4, J3.pin3, Bauteil1.A0, J6.pin_1
  N4: J2.pin1, J6.pin_0
  N5: J2.pin2, J5.pin_0
  5V: J2.pin4, Bauteil1.5V, Bauteil2.+5V
  N6: Bauteil1.D6_PWM, Bauteil2.DATAIN

custom parts:
  NeoPixel Stick: Make your own little LED strip arrangement with this stick of NeoPixel LEDs. We crammed 8 of the tiny 5050 (5mm x 5mm) smart RGB LEDs onto a PCB with mounting holes and a chainable design. Use only one microcontroller pin to control as many as you can chain together! Each LED is addressable as the driver chip is inside the LED. Each one has ~18mA constant current drive so the color will be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
